// Logisim project lab1_1_shematic.circ as structural Verilog: 1 circuit, main circuit main
module main (
  input  G,
  input  T,
  input  U,
  input  E
);

  wire E_prime_out, G_prime_out, G_prime_T_prime_UE_out, G_prime_TU_prime_E_out, G_prime_TUE_out,
       GT_prime_U_prime_E_out, GTU_prime_E_out, GTUE_out, GTUE_prime_out, or_1_out, T_prime_out, U_prime_out;

  not G_prime (G_prime_out, G);
  not E_prime (E_prime_out, E);
  not U_prime (U_prime_out, U);
  not T_prime (T_prime_out, T);
  and G_prime_T_prime_UE (G_prime_T_prime_UE_out, G_prime_out, T_prime_out, U, E);
  and G_prime_TU_prime_E (G_prime_TU_prime_E_out, G_prime_out, T, U_prime_out, E);
  and G_prime_TUE (G_prime_TUE_out, G_prime_out, T, U, E);
  and GT_prime_U_prime_E (GT_prime_U_prime_E_out, G, T_prime_out, U_prime_out, E);
  and GTU_prime_E (GTU_prime_E_out, G, T, U_prime_out, E);
  and GTUE_prime (GTUE_prime_out, G, T, U, E_prime_out);
  and GTUE (GTUE_out, G, T, U, E);
  or or_1 (or_1_out, G_prime_T_prime_UE_out, G_prime_TU_prime_E_out, G_prime_TUE_out, GT_prime_U_prime_E_out, GTU_prime_E_out, GTUE_prime_out, GTUE_out);
  // Probe on or_1_out
endmodule
