// Logisim project lab1_2_shematic.circ as structural Verilog: 1 circuit, main circuit main
module main (
  input  G,
  input  T,
  input  U,
  input  E
);

  wire G_prime_out, G_prime_UE_out, GTU_out, GU_prime_E_out, or_1_out, TE_out, U_prime_out;

  not G_prime (G_prime_out, G);
  not U_prime (U_prime_out, U);
  and G_prime_UE (G_prime_UE_out, G_prime_out, U, E);
  and TE (TE_out, T, E);
  and GU_prime_E (GU_prime_E_out, G, U_prime_out, E);
  and GTU (GTU_out, G, T, U);
  // Probe on or_1_out
  or or_1 (or_1_out, G_prime_UE_out, TE_out, GU_prime_E_out, GTU_out);
endmodule
