// Logisim project lab1_3_shematic.circ as structural Verilog: 1 circuit, main circuit main
module main (
  input  G,
  input  T,
  input  U,
  input  E,
  input  G_2,
  input  T_2,
  input  U_2,
  input  E_2
);

  wire and_1_out, not_1_out, not_2_out, not_3_out, not_4_out, or_1_out, or_2_out;

  not not_1 (not_1_out, G_2);
  not not_2 (not_2_out, E);
  not not_3 (not_3_out, T);
  not not_4 (not_4_out, U_2);
  and and_1 (and_1_out, not_2_out, or_1_out);
  or or_1 (or_1_out, U, not_3_out);
  or or_2 (or_2_out, not_4_out, not_1_out);
  // Probe on or_2_out
  // Probe on and_1_out
endmodule
